// Logisim project ID_EX_Regi.circ as structural Verilog: 1 circuit, main circuit ID/EX
module ID_EX (
  input  [7:0] Next_Pc,
  input  [9:0] ALUSrc_BN_B_MemToReg_MW_MR_RW_RD_S_J,
  input  [11:0] RS_RT_RD,
  input  [23:0] VALUES_RS_RD_RT_IM,
  input  [2:0] ALU_OP,
  input  CLR,
  input  Clock,
  output [7:0] Next_Pc_2,
  output [9:0] ALUSrc_BN_B_MemToReg_MW_MR_RW_RD_S_J_2,
  output [11:0] RS_RT_RD_2,
  output [23:0] VALUES_RS_RD_RT_IM_2,
  output [2:0] ALU_OP_2
);

  Register #(.width(30)) register_1 (
    .D({RS_RT_RD, ALUSrc_BN_B_MemToReg_MW_MR_RW_RD_S_J, Next_Pc}), .en(1'b1),
    .Q({RS_RT_RD_2, ALUSrc_BN_B_MemToReg_MW_MR_RW_RD_S_J_2, Next_Pc_2}), .clk(Clock), .clr(CLR));
  Register #(.width(27)) register_2 (
    .D({ALU_OP, VALUES_RS_RD_RT_IM}), .en(1'b1), .Q({ALU_OP_2, VALUES_RS_RD_RT_IM_2}), .clk(Clock), .clr(CLR));

  // Notes on the sheet:
  //   Register Numbers
  //   RD= RegDst S = Shift 
  //   J means Jump , MR = MEMORY Read  ,BN = bneq,B= beq
endmodule
